// Logisim project PROJETO.circ as structural Verilog
module ADD_1 (
  input  a,
  input  b,
  input  Vem_1,
  output S,
  output vai_1
);

  wire and_1_out, and_2_out, or_1_out, xor_1_out;

  xor xor_1 (xor_1_out, b, a);
  or or_1 (or_1_out, Vem_1, b);
  and and_1 (and_1_out, b, Vem_1);
  and and_2 (and_2_out, or_1_out, a);
  xor xor_2 (S, Vem_1, xor_1_out);
  or or_2 (vai_1, and_2_out, and_1_out);
endmodule

module add_4 (
  input  [3:0] in_1,
  input  [3:0] in_2,
  output out_3,
  output [3:0] out_4
);

  wire add_1_2_vai_1, add_1_3_vai_1, add_1_4_vai_1;

  ADD_1 add_1_1 (.S(out_4[3]), .vai_1(out_3), .a(in_2[3]), .b(in_1[3]), .Vem_1(add_1_2_vai_1));
  ADD_1 add_1_2 (.S(out_4[2]), .vai_1(add_1_2_vai_1), .a(in_2[2]), .b(in_1[2]), .Vem_1(add_1_3_vai_1));
  ADD_1 add_1_3 (.S(out_4[1]), .vai_1(add_1_3_vai_1), .a(in_2[1]), .b(in_1[1]), .Vem_1(add_1_4_vai_1));
  ADD_1 add_1_4 (.S(out_4[0]), .vai_1(add_1_4_vai_1), .a(in_2[0]), .b(in_1[0]), .Vem_1(1'b0));
endmodule

module comp2 (
  input  [3:0] in_1,
  output [3:0] out_2
);

  wire [3:0] not_4_out;

  not not_1 (not_4_out[3], in_1[3]);
  not not_2 (not_4_out[1], in_1[1]);
  not not_3 (not_4_out[2], in_1[2]);
  not not_4 (not_4_out[0], in_1[0]);
  add_4 add_4_1 (.in_2(not_4_out), .in_1(4'b0001), .out_4(out_2));  // open: out_3
endmodule

module sub (
  input  [3:0] B,
  input  [3:0] A,
  output [3:0] out_3
);

  wire [3:0] comp2_1_out_2;

  comp2 comp2_1 (.in_1(B), .out_2(comp2_1_out_2));
  add_4 add_4_1 (.in_2(A), .in_1(comp2_1_out_2), .out_4(out_3));  // open: out_3
endmodule

module jogo (
  input  a,
  input  b,
  input  c,
  input  d,
  output S
);

  wire and_1_out, and_2_out, and_3_out, and_4_out, and_5_out, not_1_out, not_2_out, not_3_out, not_4_out;

  not not_1 (not_1_out, a);
  not not_2 (not_2_out, b);
  not not_3 (not_3_out, c);
  not not_4 (not_4_out, d);
  and and_1 (and_1_out, not_1_out, b, c, d);
  and and_2 (and_2_out, a, not_2_out, c, d);
  and and_3 (and_3_out, a, b, not_3_out, d);
  and and_4 (and_4_out, a, b, c, not_4_out);
  and and_5 (and_5_out, a, b, c, d);
  or or_1 (S, and_1_out, and_2_out, and_3_out, and_4_out, and_5_out);
endmodule

module clock (
  output [3:0] out_1,
  output [3:0] out_2,
  output [3:0] out_3,
  output [3:0] out_4,
  output [3:0] out_5,
  output [3:0] out_6
);

  wire and_1_out, and_2_out, and_3_out, and_4_out, and_5_out, and_6_out, and_7_out, and_8_out, clock_1_out,
       or_1_out;

  Counter #(.width(4), .max('hf)) counter_1 (
    .Q(out_1), .clk(and_4_out), .clr(and_3_out));  // open: load, D, count, carry
  and and_1 (and_1_out, ~out_1[3], ~out_1[2], out_1[1], ~out_1[0]);  // AND_Gate
  and and_2 (and_2_out, ~out_2[3], out_2[2], ~out_2[1], ~out_2[0]);  // AND_Gate
  and and_3 (and_3_out, and_1_out, and_2_out);
  Counter #(.width(4), .max('hb)) counter_2 (
    .Q(out_2), .clk(and_5_out), .clr(or_1_out));  // open: load, D, count, carry
  and and_4 (and_4_out, out_2[3], ~out_2[2], out_2[1], ~out_2[0]);  // AND_Gate
  or or_1 (or_1_out, and_3_out, and_4_out);
  Counter #(.width(4), .max('hf)) counter_3 (
    .Q(out_3), .clk(and_6_out), .clr(and_5_out));  // open: load, D, count, carry
  and and_5 (and_5_out, ~out_3[3], out_3[2], out_3[1], ~out_3[0]);  // AND_Gate
  Counter #(.width(4), .max('hb)) counter_4 (
    .Q(out_4), .clk(and_7_out), .clr(and_6_out));  // open: load, D, count, carry
  and and_6 (and_6_out, out_4[3], ~out_4[2], out_4[1], ~out_4[0]);  // AND_Gate
  Counter #(.width(4), .max('hf)) counter_5 (
    .Q(out_5), .clk(and_8_out), .clr(and_7_out));  // open: load, D, count, carry
  and and_7 (and_7_out, ~out_5[3], out_5[2], out_5[1], ~out_5[0]);  // AND_Gate
  Counter #(.width(4), .max('hb)) counter_6 (
    .Q(out_6), .clk(clock_1_out), .clr(and_8_out));  // open: load, D, count, carry
  Clock clock_1 (.out(clock_1_out));
  and and_8 (and_8_out, out_6[3], ~out_6[2], out_6[1], ~out_6[0]);  // AND_Gate
endmodule

module clock_2_0 (
);

  wire [3:0] clock_1_out_1, clock_1_out_2, clock_1_out_3, clock_1_out_4, clock_1_out_5, clock_1_out_6;

  Hex_Digit_Display hex_digit_display_1 (.value(clock_1_out_2));  // open: dp
  Hex_Digit_Display hex_digit_display_2 (.value(clock_1_out_1));  // open: dp
  Hex_Digit_Display hex_digit_display_3 (.value(clock_1_out_3));  // open: dp
  clock clock_1 (
    .out_1(clock_1_out_1), .out_2(clock_1_out_2), .out_3(clock_1_out_3), .out_4(clock_1_out_4),
    .out_5(clock_1_out_5), .out_6(clock_1_out_6));
  Hex_Digit_Display hex_digit_display_4 (.value(clock_1_out_5));  // open: dp
  Hex_Digit_Display hex_digit_display_5 (.value(clock_1_out_4));  // open: dp
  Hex_Digit_Display hex_digit_display_6 (.value(clock_1_out_6));  // open: dp
endmodule
